# Fritzing sketch S2 (saved by Fritzing 0.9.5d)

parts:
  U1 = ESP32-38PinWide [part_number=ESP32-38PinWide]  # not connected
  M4 = Stepper Motor - Bipolar
  A1 = A4988 driver expansion card
  A2 = A4988 driver expansion card
  M5 = Stepper Motor - Bipolar
  A3 = ESP32 devkit 38p expansion board
  Boost_Convertor1 = Boost Convertor [part_number=XL6009E1 package=THT]
  VCC1 = Battery
  Mod3 = TMC2209 [package=THT]  # not connected
  Mod4 = TMC2209 [package=THT]  # not connected
  Power_plug1 = Power plug
  S2 = Pushbutton [package="[THT]"]
  S3 = Pushbutton [package="[THT]"]
  S5 = Pushbutton [package="[THT]"]
  M6 = lcd color display 0.96in 80x160 8pin interface [package=THT]
  Part1 = InvenSense MPU6050

nets:
  N1: M4.A, A2.Pin_10
  N2: M4.C, A2.Pin_11
  N3: M4.B, A2.Pin_12
  N4: M4.D, A2.Pin_13
  N5: A1.Pin_3, A1.Pin_14, A2.Pin_14, Boost_Convertor1.Negative_Output
  VCC: A1.Pin_4, A1.Pin_6, A2.Pin_4, A2.Pin_6, A3.Pin_23, A3.Pin_28, A3.Pin_30, A3.Pin_160, A3.Pin_161, M6.VCC, Part1.VCC
  N6: A1.Pin_7, A3.Pin_11, A3.Pin_90
  N7: A1.Pin_8, A3.Pin_10, A3.Pin_89
  N8: A1.Pin_9, A3.Pin_9, A3.Pin_88
  N9: A1.Pin_10, M5.D
  N10: A1.Pin_11, M5.B
  N11: A1.Pin_12, M5.C
  N12: A1.Pin_13, M5.A
  N13: A1.Pin_15, A2.Pin_15, Boost_Convertor1.Positive_Output
  N14: A2.Pin_7, A3.Pin_8
  N15: A2.Pin_8, A3.Pin_7
  N16: A2.Pin_9, A3.Pin_6
  N17: A3.Pin_1, A3.Pin_80, S3.Pin_1, S3.Pin_2
  N18: A3.Pin_12, S2.Pin_1, S2.Pin_2
  N19: A3.Pin_13, S5.Pin_3
  GND: A3.Pin_35, A3.Pin_46, A3.Pin_47, A3.Pin_73, A3.Pin_143, A3.Pin_144, S2.Pin_3, S2.Pin_4, S3.Pin_3, S5.Pin_1, S5.Pin_2, M6.GND, Part1.GND
  N20: A3.Pin_114, A3.Pin_174, Part1.SDA
  N21: A3.Pin_117, A3.Pin_177, Part1.SCL
  N22: A3.Pin_165, M6.CS
  N23: A3.Pin_166, M6.DC
  N24: A3.Pin_168, M6.RES
  N25: A3.Pin_172, M6.SCL
  N26: A3.Pin_178, M6.SDA
  N27: Boost_Convertor1.Negative_Input, Power_plug1.GND
  N28: Boost_Convertor1.Positive_Input, VCC1.+, Power_plug1.VCC

notes:
  // left stepper
  #define DIR1 26
  #define STEP1 27
  #define EN1 14
  // right stepper
  #define DIR2 32
  #define STEP2 33
  #define EN2 25
  Output: 12V
  Motor driver VREF: 0.52-0.55V
  Micro stepping: 1/16
  - MS1 - on
  - MS2 - on
  // buttons
  Start button: 13
  mode button: 12
  Reset button: EN/RESET
  // display
  SCL: 18
  SDA: 23
  RES: 4
  DC: 2
  CB: 15
  // Gyro
  SCL: 22
  SDA: 21
  Note: the part in diagram is different from the actual part, pin order is different.

custom parts:
  ESP32-38PinWide: Generic 38-Pin ESP32 with wide format (only access to one side of pins on a breadboard) based on Stephen Lilley's HiLetgo ESP-WROOM-32 ESP32 ESP-32S Development Board.
  A4988 driver expansion card: A4988 driver expansion card.
  ESP32 devkit 38p expansion board: Upgraded ESP32 38P Development ESP32-DevKitC-32 ESP-WROOM-32 Expansion Board.
  Boost Convertor: DC to DC boost convertor
  TMC2209: TMC2209-LA stepper motor controller and driver. Supply voltage 4.75-28V Iphase up to 1.77A rms (2.5A peak)
  lcd color display 0.96in 80x160 8pin interface: Ips 0.96 Inch 8 Pin Spi Hd 65K Full Color Tft Module St7735 Drive Ic 80 x 160 Lcd Display 3.3V Spi Interface.
